# Fritzing sketch medium fritz board (saved by Fritzing 0.9.9b)
breadboards: 1

parts:
  Teensy1 = Teensy 3.0
  WIZ820io1 = WIZ820io [part_number=WIZ820io]
  Part1 = Breakout Board for Electret Microphone
  Part2 = Adafruit MicroSD card breakout board [part_number="Adafruit #254"]
  RG_encoder1 = SprkFn RG Encoder [package="DIP (Dual Inline) [THT]"]

nets:
  GND: Teensy1.GND, WIZ820io1.GND, Part1.GND
  N1: Teensy1.D3, Part2.CS
  N2: Teensy1.D9, WIZ820io1.nRESET
  N3: Teensy1.D10, WIZ820io1.nSS
  N4: Teensy1.D11, WIZ820io1.MOSI, Part2.DI
  N5: Teensy1.D12, WIZ820io1.MISO, Part2.DO
  N6: Teensy1.D13, WIZ820io1.SCLK, Part2.CLK
  N7: Teensy1.A0/D14, Teensy1.A1/D15, Teensy1.A2/D16
  N8: Teensy1.A5/D19, Part1.AUD
  VIN: Teensy1.Vin, Part2.VCC
  VIN_2: WIZ820io1.VIN, Part1.VCC
  N9: RG_encoder1.+R, RG_encoder1.+G, RG_encoder1.SW, RG_encoder1.GND
  N10: RG_encoder1.A, RG_encoder1.B, RG_encoder1.C

custom parts:
  Adafruit MicroSD card breakout board: Not just a simple breakout board, this microSD adapter goes the extra mile - designed for ease of use. Onboard 5v->3v regulator provides 150mA for power-hungry cards 3v level shifting means you can use this with ease on either 3v or 5v systems Uses a proper level shifting chip, not resistors: less problems, and faster read/write access Use 3 or 4 digital pins to read and write 2Gb+ of storage!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
  SprkFn RG Encoder: SparkFun RG Rotary Encoder
